// Logisim project BIT-REGISTER.circ as structural Verilog
module \bit  (
  input  in,
  input  load,
  output out
);

  wire multiplexer_1_out;

  Multiplexer multiplexer_1 (.in0(out), .in1(in), .out(multiplexer_1_out), .sel(load));  // open: en
  D_Flip_Flop d_ff_1 (.D(multiplexer_1_out), .Q(out));  // open: clk, Qn, preset, en, reset
endmodule

module register (
  input  load,
  input  [15:0] in,
  output [15:0] out
);

  \bit  bit_1 (.in(in[0]), .load(load), .out(out[0]));
  \bit  bit_2 (.in(in[1]), .load(load), .out(out[1]));
  \bit  bit_3 (.in(in[2]), .load(load), .out(out[2]));
  \bit  bit_4 (.in(in[3]), .load(load), .out(out[3]));
  \bit  bit_5 (.in(in[5]), .load(load), .out(out[5]));
  \bit  bit_6 (.in(in[8]), .load(load), .out(out[8]));
  \bit  bit_7 (.in(in[9]), .load(load), .out(out[9]));
  \bit  bit_8 (.in(in[14]), .load(load), .out(out[14]));
  \bit  bit_9 (.in(in[15]), .load(load), .out(out[15]));
  \bit  bit_10 (.in(in[4]), .load(load), .out(out[4]));
  \bit  bit_11 (.in(in[6]), .load(load), .out(out[6]));
  \bit  bit_12 (.in(in[7]), .load(load), .out(out[7]));
  \bit  bit_13 (.in(in[10]), .load(load), .out(out[10]));
  \bit  bit_14 (.in(in[11]), .load(load), .out(out[11]));
  \bit  bit_15 (.in(in[12]), .load(load), .out(out[12]));
  \bit  bit_16 (.in(in[13]), .load(load), .out(out[13]));
endmodule
