// Logisim project Mux4way16yMux8way16defi.circ as structural Verilog: 2 circuits, main circuit Mux4Way16
module Mux4Way16 (
  input  [15:0] a,
  input  [15:0] b,
  input  [15:0] c,
  input  [15:0] d,
  input  [1:0] in_5,
  output [15:0] out
);

  wire [15:0] multiplexer_1_out, multiplexer_2_out;

  Multiplexer #(.width(16), .enable("false")) multiplexer_1 (.in0(a), .in1(b), .out(multiplexer_1_out), .sel(in_5[0]));
  Multiplexer #(.width(16), .enable("false")) multiplexer_2 (.in0(c), .in1(d), .out(multiplexer_2_out), .sel(in_5[0]));
  Multiplexer #(.width(16), .enable("false")) multiplexer_3 (
    .in0(multiplexer_1_out), .in1(multiplexer_2_out), .out(out), .sel(in_5[1]));
endmodule

module Mux8Way16 (
  input  [15:0] in_1,
  input  [15:0] in_2,
  input  [15:0] in_3,
  input  [15:0] in_4,
  input  [15:0] in_5,
  input  [15:0] in_6,
  input  [15:0] in_7,
  input  [15:0] in_8,
  input  [2:0] in_9,
  output [15:0] out_10
);

  wire [15:0] mux4way16_1_out, mux4way16_2_out;

  Mux4Way16 mux4way16_1 (.a(in_1), .b(in_2), .c(in_3), .d(in_4), .in_5(in_9[1:0]), .out(mux4way16_1_out));
  Mux4Way16 mux4way16_2 (.a(in_5), .b(in_6), .c(in_7), .d(in_8), .in_5(in_9[1:0]), .out(mux4way16_2_out));
  Multiplexer #(.width(16), .enable("false")) multiplexer_1 (
    .in0(mux4way16_1_out), .in1(mux4way16_2_out), .out(out_10), .sel(in_9[2]));
endmodule
