// Logisim project RAM64.circ as structural Verilog: 2 circuits, main circuit main
module main (
  input  [15:0] inn,
  input  WE,
  input  [5:0] ADDRESS,
  output [15:0] OUTT
);

  wire clock_1_out, demultiplexer_1_out0, demultiplexer_1_out1, demultiplexer_1_out2, demultiplexer_1_out3,
       demultiplexer_1_out4, demultiplexer_1_out5, demultiplexer_1_out6;
  wire [15:0] ram8_1_oout, ram8_2_oout, ram8_3_oout, ram8_4_oout, ram8_5_oout, ram8_6_oout, ram8_7_oout,
       ram8_8_oout;

  Clock clock_1 (.out(clock_1_out));
  RAM8 ram8_1 (.CLCK(clock_1_out), .INN(inn), .load(demultiplexer_1_out0), .address(ADDRESS[2:0]), .OOUT(ram8_1_oout));
  RAM8 ram8_2 (.CLCK(clock_1_out), .INN(inn), .load(demultiplexer_1_out1), .address(ADDRESS[2:0]), .OOUT(ram8_2_oout));
  RAM8 ram8_3 (.CLCK(clock_1_out), .INN(inn), .load(demultiplexer_1_out2), .address(ADDRESS[2:0]), .OOUT(ram8_3_oout));
  RAM8 ram8_4 (.CLCK(clock_1_out), .INN(inn), .load(demultiplexer_1_out3), .address(ADDRESS[2:0]), .OOUT(ram8_4_oout));
  RAM8 ram8_5 (.CLCK(clock_1_out), .INN(inn), .load(demultiplexer_1_out4), .address(ADDRESS[2:0]), .OOUT(ram8_5_oout));
  RAM8 ram8_6 (.CLCK(clock_1_out), .INN(inn), .load(demultiplexer_1_out5), .address(ADDRESS[2:0]), .OOUT(ram8_6_oout));
  RAM8 ram8_7 (.CLCK(clock_1_out), .INN(inn), .load(demultiplexer_1_out6), .address(ADDRESS[2:0]), .OOUT(ram8_7_oout));
  RAM8 ram8_8 (.CLCK(clock_1_out), .INN(inn), .load(demultiplexer_1_out6), .address(ADDRESS[2:0]), .OOUT(ram8_8_oout));
  Demultiplexer #(.select(3)) demultiplexer_1 (
    .out0(demultiplexer_1_out0), .out1(demultiplexer_1_out1), .out2(demultiplexer_1_out2),
    .out3(demultiplexer_1_out3), .out4(demultiplexer_1_out4), .out5(demultiplexer_1_out5),
    .out6(demultiplexer_1_out6), .out7(demultiplexer_1_out6), .in(WE), .sel(ADDRESS[5:3]));
  Multiplexer #(.select(3), .width(16)) multiplexer_1 (
    .in0(ram8_1_oout), .in1(ram8_2_oout), .in2(ram8_3_oout), .in3(ram8_4_oout), .in4(ram8_5_oout),
    .in5(ram8_6_oout), .in6(ram8_7_oout), .in7(ram8_8_oout), .out(OUTT), .sel(ADDRESS[5:3]));
endmodule

module RAM8 (
  input  CLCK,
  input  [15:0] INN,
  input  load,
  input  [2:0] address,
  output [15:0] OOUT
);

  wire demultiplexer_1_out0, demultiplexer_1_out1, demultiplexer_1_out2, demultiplexer_1_out3,
       demultiplexer_1_out4, demultiplexer_1_out5, demultiplexer_1_out6, demultiplexer_1_out7;
  wire [15:0] register_1_q, register_2_q, register_3_q, register_4_q, register_5_q, register_6_q,
       register_7_q, register_8_q;

  Demultiplexer #(.select(3)) demultiplexer_1 (
    .out0(demultiplexer_1_out0), .out1(demultiplexer_1_out1), .out2(demultiplexer_1_out2),
    .out3(demultiplexer_1_out3), .out4(demultiplexer_1_out4), .out5(demultiplexer_1_out5),
    .out6(demultiplexer_1_out6), .out7(demultiplexer_1_out7), .in(load), .sel(address));
  Register #(.width(16)) register_1 (.D(INN), .en(demultiplexer_1_out0), .clk(CLCK), .Q(register_1_q));  // open: clr
  Register #(.width(16)) register_2 (.D(INN), .en(demultiplexer_1_out1), .clk(CLCK), .Q(register_2_q));  // open: clr
  Register #(.width(16)) register_3 (.D(INN), .en(demultiplexer_1_out2), .clk(CLCK), .Q(register_3_q));  // open: clr
  Register #(.width(16)) register_4 (.D(INN), .en(demultiplexer_1_out3), .clk(CLCK), .Q(register_4_q));  // open: clr
  Register #(.width(16)) register_5 (.D(INN), .en(demultiplexer_1_out4), .clk(CLCK), .Q(register_5_q));  // open: clr
  Register #(.width(16)) register_6 (.D(INN), .en(demultiplexer_1_out5), .clk(CLCK), .Q(register_6_q));  // open: clr
  Register #(.width(16)) register_7 (.D(INN), .en(demultiplexer_1_out6), .clk(CLCK), .Q(register_7_q));  // open: clr
  Register #(.width(16)) register_8 (.D(INN), .en(demultiplexer_1_out7), .clk(CLCK), .Q(register_8_q));  // open: clr
  Clock clock_1 (.out(CLCK));
  Multiplexer #(.select(3), .width(16)) multiplexer_1 (
    .in0(register_1_q), .in1(register_2_q), .in2(register_3_q), .in3(register_4_q), .in4(register_5_q),
    .in5(register_6_q), .in6(register_7_q), .in7(register_8_q), .out(OOUT), .sel(address));
endmodule
