// Logisim project RAM64_512_4K_16K.circ as structural Verilog: 5 circuits, main circuit main
module main (
  input  clck,
  input  [15:0] inn,
  input  WE,
  input  [5:0] ADDRESS,
  output [15:0] OUTT
);

  wire demultiplexer_1_out0, demultiplexer_1_out1, demultiplexer_1_out2, demultiplexer_1_out3,
       demultiplexer_1_out4, demultiplexer_1_out5, demultiplexer_1_out6;
  wire [15:0] ram8_1_oout, ram8_2_oout, ram8_3_oout, ram8_4_oout, ram8_5_oout, ram8_6_oout, ram8_7_oout,
       ram8_8_oout;

  Clock clock_1 (.out(clck));
  RAM8 ram8_1 (.CLCK(clck), .INN(inn), .load(demultiplexer_1_out0), .address(ADDRESS[2:0]), .OOUT(ram8_1_oout));
  RAM8 ram8_2 (.CLCK(clck), .INN(inn), .load(demultiplexer_1_out1), .address(ADDRESS[2:0]), .OOUT(ram8_2_oout));
  RAM8 ram8_3 (.CLCK(clck), .INN(inn), .load(demultiplexer_1_out2), .address(ADDRESS[2:0]), .OOUT(ram8_3_oout));
  RAM8 ram8_4 (.CLCK(clck), .INN(inn), .load(demultiplexer_1_out3), .address(ADDRESS[2:0]), .OOUT(ram8_4_oout));
  RAM8 ram8_5 (.CLCK(clck), .INN(inn), .load(demultiplexer_1_out4), .address(ADDRESS[2:0]), .OOUT(ram8_5_oout));
  RAM8 ram8_6 (.CLCK(clck), .INN(inn), .load(demultiplexer_1_out5), .address(ADDRESS[2:0]), .OOUT(ram8_6_oout));
  RAM8 ram8_7 (.CLCK(clck), .INN(inn), .load(demultiplexer_1_out6), .address(ADDRESS[2:0]), .OOUT(ram8_7_oout));
  RAM8 ram8_8 (.CLCK(clck), .INN(inn), .load(demultiplexer_1_out6), .address(ADDRESS[2:0]), .OOUT(ram8_8_oout));
  Demultiplexer #(.select(3)) demultiplexer_1 (
    .out0(demultiplexer_1_out0), .out1(demultiplexer_1_out1), .out2(demultiplexer_1_out2),
    .out3(demultiplexer_1_out3), .out4(demultiplexer_1_out4), .out5(demultiplexer_1_out5),
    .out6(demultiplexer_1_out6), .out7(demultiplexer_1_out6), .in(WE), .sel(ADDRESS[5:3]));
  Multiplexer #(.select(3), .width(16)) multiplexer_1 (
    .in0(ram8_1_oout), .in1(ram8_2_oout), .in2(ram8_3_oout), .in3(ram8_4_oout), .in4(ram8_5_oout),
    .in5(ram8_6_oout), .in6(ram8_7_oout), .in7(ram8_8_oout), .out(OUTT), .sel(ADDRESS[5:3]));
endmodule

module RAM8 (
  input  CLCK,
  input  [15:0] INN,
  input  load,
  input  [2:0] address,
  output [15:0] OOUT
);

  wire demultiplexer_1_out0, demultiplexer_1_out1, demultiplexer_1_out2, demultiplexer_1_out3,
       demultiplexer_1_out4, demultiplexer_1_out5, demultiplexer_1_out6, demultiplexer_1_out7;
  wire [15:0] register_1_q, register_2_q, register_3_q, register_4_q, register_5_q, register_6_q,
       register_7_q, register_8_q;

  Demultiplexer #(.select(3)) demultiplexer_1 (
    .out0(demultiplexer_1_out0), .out1(demultiplexer_1_out1), .out2(demultiplexer_1_out2),
    .out3(demultiplexer_1_out3), .out4(demultiplexer_1_out4), .out5(demultiplexer_1_out5),
    .out6(demultiplexer_1_out6), .out7(demultiplexer_1_out7), .in(load), .sel(address));
  Register #(.width(16)) register_1 (.D(INN), .en(demultiplexer_1_out0), .clk(CLCK), .Q(register_1_q));  // open: clr
  Register #(.width(16)) register_2 (.D(INN), .en(demultiplexer_1_out1), .clk(CLCK), .Q(register_2_q));  // open: clr
  Register #(.width(16)) register_3 (.D(INN), .en(demultiplexer_1_out2), .clk(CLCK), .Q(register_3_q));  // open: clr
  Register #(.width(16)) register_4 (.D(INN), .en(demultiplexer_1_out3), .clk(CLCK), .Q(register_4_q));  // open: clr
  Register #(.width(16)) register_5 (.D(INN), .en(demultiplexer_1_out4), .clk(CLCK), .Q(register_5_q));  // open: clr
  Register #(.width(16)) register_6 (.D(INN), .en(demultiplexer_1_out5), .clk(CLCK), .Q(register_6_q));  // open: clr
  Register #(.width(16)) register_7 (.D(INN), .en(demultiplexer_1_out6), .clk(CLCK), .Q(register_7_q));  // open: clr
  Register #(.width(16)) register_8 (.D(INN), .en(demultiplexer_1_out7), .clk(CLCK), .Q(register_8_q));  // open: clr
  Clock clock_1 (.out(CLCK));
  Multiplexer #(.select(3), .width(16)) multiplexer_1 (
    .in0(register_1_q), .in1(register_2_q), .in2(register_3_q), .in3(register_4_q), .in4(register_5_q),
    .in5(register_6_q), .in6(register_7_q), .in7(register_8_q), .out(OOUT), .sel(address));
endmodule

module RAM512 (
  input  clck,
  input  [15:0] inn,
  input  load,
  input  [8:0] address,
  output [15:0] oout
);

  wire demultiplexer_1_out0, demultiplexer_1_out1, demultiplexer_1_out2, demultiplexer_1_out3,
       demultiplexer_1_out4, demultiplexer_1_out5, demultiplexer_1_out6, demultiplexer_1_out7;
  wire [15:0] main_1_outt, main_2_outt, main_3_outt, main_4_outt, main_5_outt, main_6_outt, main_7_outt,
       main_8_outt;

  Clock clock_1 (.out(clck));
  main main_1 (.clck(clck), .inn(inn), .WE(demultiplexer_1_out0), .ADDRESS(address[5:0]), .OUTT(main_1_outt));
  main main_2 (.clck(clck), .inn(inn), .WE(demultiplexer_1_out1), .ADDRESS(address[5:0]), .OUTT(main_2_outt));
  main main_3 (.clck(clck), .inn(inn), .WE(demultiplexer_1_out2), .ADDRESS(address[5:0]), .OUTT(main_3_outt));
  main main_4 (.clck(clck), .inn(inn), .WE(demultiplexer_1_out3), .ADDRESS(address[5:0]), .OUTT(main_4_outt));
  main main_5 (.clck(clck), .inn(inn), .WE(demultiplexer_1_out4), .ADDRESS(address[5:0]), .OUTT(main_5_outt));
  main main_6 (.clck(clck), .inn(inn), .WE(demultiplexer_1_out5), .ADDRESS(address[5:0]), .OUTT(main_6_outt));
  main main_7 (.clck(clck), .inn(inn), .WE(demultiplexer_1_out6), .ADDRESS(address[5:0]), .OUTT(main_7_outt));
  main main_8 (.clck(clck), .inn(inn), .WE(demultiplexer_1_out7), .ADDRESS(address[5:0]), .OUTT(main_8_outt));
  Demultiplexer #(.select(3)) demultiplexer_1 (
    .out0(demultiplexer_1_out0), .out1(demultiplexer_1_out1), .out2(demultiplexer_1_out2),
    .out3(demultiplexer_1_out3), .out4(demultiplexer_1_out4), .out5(demultiplexer_1_out5),
    .out6(demultiplexer_1_out6), .out7(demultiplexer_1_out7), .in(load), .sel(address[8:6]));
  Multiplexer #(.select(3), .width(16)) multiplexer_1 (
    .in0(main_1_outt), .in1(main_2_outt), .in2(main_3_outt), .in3(main_4_outt), .in4(main_5_outt),
    .in5(main_6_outt), .in6(main_7_outt), .in7(main_8_outt), .out(oout), .sel(address[8:6]));
endmodule

module RAM4K (
  input  [15:0] iin,
  input  load,
  input  [11:0] address,
  output [15:0] oout
);

  wire clock_1_out, demultiplexer_1_out0, demultiplexer_1_out1, demultiplexer_1_out2, demultiplexer_1_out3,
       demultiplexer_1_out4, demultiplexer_1_out5, demultiplexer_1_out6, demultiplexer_1_out7;
  wire [15:0] ram512_1_oout, ram512_2_oout, ram512_3_oout, ram512_4_oout, ram512_5_oout, ram512_6_oout,
       ram512_7_oout, ram512_8_oout;

  Clock clock_1 (.out(clock_1_out));
  RAM512 ram512_1 (
    .clck(clock_1_out), .inn(iin), .load(demultiplexer_1_out0), .address(address[8:0]), .oout(ram512_1_oout));
  RAM512 ram512_2 (
    .clck(clock_1_out), .inn(iin), .load(demultiplexer_1_out1), .address(address[8:0]), .oout(ram512_2_oout));
  RAM512 ram512_3 (
    .clck(clock_1_out), .inn(iin), .load(demultiplexer_1_out2), .address(address[8:0]), .oout(ram512_3_oout));
  RAM512 ram512_4 (
    .clck(clock_1_out), .inn(iin), .load(demultiplexer_1_out3), .address(address[8:0]), .oout(ram512_4_oout));
  RAM512 ram512_5 (
    .clck(clock_1_out), .inn(iin), .load(demultiplexer_1_out4), .address(address[8:0]), .oout(ram512_5_oout));
  RAM512 ram512_6 (
    .clck(clock_1_out), .inn(iin), .load(demultiplexer_1_out5), .address(address[8:0]), .oout(ram512_6_oout));
  RAM512 ram512_7 (
    .clck(clock_1_out), .inn(iin), .load(demultiplexer_1_out6), .address(address[8:0]), .oout(ram512_7_oout));
  RAM512 ram512_8 (
    .clck(clock_1_out), .inn(iin), .load(demultiplexer_1_out7), .address(address[8:0]), .oout(ram512_8_oout));
  Demultiplexer #(.select(3)) demultiplexer_1 (
    .out0(demultiplexer_1_out0), .out1(demultiplexer_1_out1), .out2(demultiplexer_1_out2),
    .out3(demultiplexer_1_out3), .out4(demultiplexer_1_out4), .out5(demultiplexer_1_out5),
    .out6(demultiplexer_1_out6), .out7(demultiplexer_1_out7), .in(load), .sel(address[11:9]));
  Multiplexer #(.select(3), .width(16)) multiplexer_1 (
    .in0(ram512_1_oout), .in1(ram512_2_oout), .in2(ram512_3_oout), .in3(ram512_4_oout), .in4(ram512_5_oout),
    .in5(ram512_6_oout), .in6(ram512_7_oout), .in7(ram512_8_oout), .out(oout), .sel(address[11:9]));
endmodule

module RAM16K (
  input  [15:0] iin,
  input  load,
  input  [13:0] address,
  output [15:0] oout
);

  wire demultiplexer_1_out0, demultiplexer_1_out1, demultiplexer_1_out2, demultiplexer_1_out3;
  wire [15:0] ram4k_1_oout, ram4k_2_oout, ram4k_3_oout, ram4k_4_oout;

  RAM4K ram4k_1 (.iin(iin), .load(demultiplexer_1_out0), .address(address[11:0]), .oout(ram4k_1_oout));
  RAM4K ram4k_2 (.iin(iin), .load(demultiplexer_1_out1), .address(address[11:0]), .oout(ram4k_2_oout));
  RAM4K ram4k_3 (.iin(iin), .load(demultiplexer_1_out2), .address(address[11:0]), .oout(ram4k_3_oout));
  RAM4K ram4k_4 (.iin(iin), .load(demultiplexer_1_out3), .address(address[11:0]), .oout(ram4k_4_oout));
  Demultiplexer #(.select(2)) demultiplexer_1 (
    .out0(demultiplexer_1_out0), .out1(demultiplexer_1_out1), .out2(demultiplexer_1_out2),
    .out3(demultiplexer_1_out3), .in(load), .sel(address[13:12]));
  Multiplexer #(.select(2), .width(16)) multiplexer_1 (
    .in0(ram4k_1_oout), .in1(ram4k_2_oout), .in2(ram4k_3_oout), .in3(ram4k_4_oout), .out(oout),
    .sel(address[13:12]));
endmodule
