// Logisim project and.circ as structural Verilog: 1 circuit, main circuit main
module main (
  input  a,
  input  b,
  output out_3
);

  wire nand_1_out, not_1_out;

  nand nand_1 (nand_1_out, a, b);
  not not_1 (not_1_out, nand_1_out);
endmodule
