// Logisim project and16.circ as structural Verilog: 1 circuit, main circuit main
module main (
  input  [15:0] a,
  input  [15:0] b,
  output [15:0] OUUT
);

  and and_1 (OUUT[0], a[0], b[0]);
  and and_2 (OUUT[1], a[1], b[1]);
  and and_3 (OUUT[2], a[2], b[2]);
  and and_4 (OUUT[3], b[3], a[3]);
  and and_5 (OUUT[4], a[4], b[4]);
  and and_6 (OUUT[5], b[5], a[5]);
  and and_7 (OUUT[6], a[6], b[6]);
  and and_8 (OUUT[7], b[7], a[7]);
  and and_9 (OUUT[8], a[8], b[8]);
  and and_10 (OUUT[9], b[9], a[9]);
  and and_11 (OUUT[10], a[10], b[10]);
  and and_12 (OUUT[11], a[11], b[11]);
  and and_13 (OUUT[12], b[12], a[12]);
  and and_14 (OUUT[13], b[13], a[13]);
  and and_15 (OUUT[14], b[14], a[14]);
  and and_16 (OUUT[15], a[15], b[15]);
endmodule
