// Logisim project dmux.circ as structural Verilog: 1 circuit, main circuit main
module main (
  input  in,
  input  sel,
  output y0,
  output y1
);

  wire and_1_out, and_2_out;

  not not_1 (in, sel);
  and and_1 (and_1_out, in, in);
  and and_2 (and_2_out, in, sel);
endmodule
