// Logisim project dmux8way.circ as structural Verilog: 1 circuit, main circuit main
module main (
  input  in_1,
  input  [2:0] sel,
  output out_3,
  output out_4,
  output out_5,
  output out_6,
  output out_7,
  output out_8,
  output out_9,
  output out_10
);

  wire demultiplexer_1_out0, demultiplexer_1_out1;

  Demultiplexer demultiplexer_1 (.out0(demultiplexer_1_out0), .out1(demultiplexer_1_out1), .in(in_1), .sel(sel[2]));
  Demultiplexer #(.select(2)) demultiplexer_2 (
    .out0(out_7), .out1(out_8), .out2(out_9), .out3(out_10), .in(demultiplexer_1_out1), .sel(sel[1:0]));
  Demultiplexer #(.select(2)) demultiplexer_3 (
    .out0(out_3), .out1(out_4), .out2(out_5), .out3(out_6), .in(demultiplexer_1_out0), .sel(sel[1:0]));
endmodule
