// Logisim project mux16.circ as structural Verilog: 1 circuit, main circuit main
module main (
  input  sel,
  input  [15:0] a,
  input  [15:0] b,
  output [15:0] out_4
);

  Multiplexer multiplexer_1 (.in0(a[0]), .in1(b[0]), .out(out_4[0]), .sel(sel));
  Multiplexer multiplexer_2 (.in0(a[1]), .in1(b[1]), .out(out_4[1]), .sel(sel));
  Multiplexer multiplexer_3 (.in0(a[2]), .in1(b[2]), .out(out_4[2]), .sel(sel));
  Multiplexer multiplexer_4 (.in0(a[3]), .in1(b[3]), .out(out_4[3]), .sel(sel));
  Multiplexer multiplexer_5 (.in0(a[4]), .in1(b[4]), .out(out_4[4]), .sel(sel));
  Multiplexer multiplexer_6 (.in0(a[5]), .in1(b[5]), .out(out_4[5]), .sel(sel));
  Multiplexer multiplexer_7 (.in0(a[6]), .in1(b[6]), .out(out_4[6]), .sel(sel));
  Multiplexer multiplexer_8 (.in0(a[7]), .in1(b[7]), .out(out_4[7]), .sel(sel));
  Multiplexer multiplexer_9 (.in0(a[8]), .in1(b[8]), .out(out_4[8]), .sel(sel));
  Multiplexer multiplexer_10 (.in0(a[9]), .in1(b[9]), .out(out_4[9]), .sel(sel));
  Multiplexer multiplexer_11 (.in0(a[10]), .in1(b[10]), .out(out_4[10]), .sel(sel));
  Multiplexer multiplexer_12 (.in0(a[11]), .in1(b[11]), .out(out_4[11]), .sel(sel));
  Multiplexer multiplexer_13 (.in0(a[12]), .in1(b[12]), .out(out_4[12]), .sel(sel));
  Multiplexer multiplexer_14 (.in0(a[15]), .in1(b[13]), .out(out_4[13]), .sel(sel));
  Multiplexer multiplexer_15 (.in0(a[14]), .in1(b[14]), .out(out_4[14]), .sel(sel));
  Multiplexer multiplexer_16 (.in0(a[15]), .in1(b[15]), .out(out_4[15]), .sel(sel));

  assign a[13] = a[15];
endmodule
