// Logisim project or16.circ as structural Verilog: 1 circuit, main circuit main
module main (
  input  [15:0] a,
  input  [15:0] b,
  output [15:0] OOUT
);

  or or_1 (OOUT[0], a[0], b[0]);
  or or_2 (OOUT[1], a[1], b[1]);
  or or_3 (OOUT[2], a[2], b[2]);
  or or_4 (OOUT[3], a[3], b[3]);
  or or_5 (OOUT[4], a[4], b[4]);
  or or_6 (OOUT[5], a[5], b[5]);
  or or_7 (OOUT[6], a[6], b[6]);
  or or_8 (OOUT[7], a[7], b[7]);
  or or_9 (OOUT[8], a[8], b[8]);
  or or_10 (OOUT[9], a[9], b[9]);
  or or_11 (OOUT[10], b[10], a[10]);
  or or_12 (OOUT[11], b[11], a[11]);
  or or_13 (OOUT[12], a[12], b[12]);
  or or_14 (OOUT[13], a[13], b[13]);
  or or_15 (OOUT[14], b[14], a[14]);
  or or_16 (OOUT[15], b[15], a[15]);
endmodule
