// Logisim project or8way.circ as structural Verilog: 1 circuit, main circuit main
module main (
  input  [7:0] in_1,
  output out_2
);

  wire or_1_out, or_2_out, or_3_out, or_5_out, or_6_out, or_7_out;

  or or_1 (or_1_out, in_1[0], in_1[1]);
  or or_2 (or_2_out, in_1[2], in_1[3]);
  or or_3 (or_3_out, or_1_out, or_2_out);
  or or_4 (out_2, or_3_out, or_6_out);
  or or_5 (or_5_out, in_1[4], in_1[5]);
  or or_6 (or_6_out, or_5_out, or_7_out);
  or or_7 (or_7_out, in_1[6], in_1[7]);
endmodule
