// Logisim project sum4def.circ as structural Verilog
module half (
  input  A,
  input  B,
  output sum,
  output carry
);

  xor xor_1 (sum, A, B);
  and and_1 (carry, A, B);
endmodule

module full (
  input  A,
  input  B,
  input  carryIn,
  output sum,
  output carryOut
);

  wire and_1_out, and_2_out, xor_1_out;

  xor xor_1 (xor_1_out, A, B);
  and and_1 (and_1_out, A, B);
  xor xor_2 (sum, xor_1_out, carryIn);
  and and_2 (and_2_out, carryIn, xor_1_out);
  or or_1 (carryOut, and_2_out, and_1_out);
endmodule

module sum4 (
  input  A4,
  input  A3,
  input  A2,
  input  A1,
  input  B4,
  input  B3,
  input  B2,
  input  B1,
  output COUT,
  output O4,
  output O3,
  output O2,
  output O1
);

  wire full_2_carryout, full_3_carryout, half_1_carry;

  full full_1 (.A(A4), .B(B4), .carryIn(full_2_carryout), .sum(O4), .carryOut(COUT));
  full full_2 (.A(A3), .B(B3), .carryIn(full_3_carryout), .sum(O3), .carryOut(full_2_carryout));
  full full_3 (.A(A2), .B(B2), .carryIn(half_1_carry), .sum(O2), .carryOut(full_3_carryout));
  half half_1 (.A(A1), .B(B1), .sum(O1), .carry(half_1_carry));
endmodule
