// Logisim project sumadorcompleto.circ as structural Verilog: 1 circuit, main circuit main
module main (
  input  x,
  input  y,
  input  carryin,
  output out_4,
  output out_5
);

  wire and_1_out, and_2_out, or_1_out, xor_1_out, xor_2_out;

  and and_1 (and_1_out, x, y);
  xor xor_1 (xor_1_out, x, y);
  xor xor_2 (xor_2_out, xor_1_out, carryin);
  and and_2 (and_2_out, xor_1_out, carryin);
  or or_1 (or_1_out, and_1_out, and_2_out);
endmodule
